# Fritzing sketch SketchBoitier_v1 (saved by Fritzing 0.9.2b)

parts:
  VCC1 = Battery block 9V
  BAT1 = Battery Holders [package=battery-aa]
  Composant1 = LilyPad Slide Switch
  LED1 = LED - 5mm [color="Red (633nm)" package="5 mm [THT]"]
  U1 = RELAY [package=relay-g5q]
  U2 = RELAY [package=relay-g5q]
  U3 = RELAY [package=relay-g5q]
  U4 = RELAY [package=relay-g5q]
  U5 = RELAY [package=relay-g5q]
  Composant2 = Arduino Mega ADK (Rev3)
  R1 = Resistor [tolerance=±5% resistance=220 package="0805 [SMD]"]
  Composant3 = Arduino Xbee Libellium Shield
  R2 = Resistor [tolerance=±5% resistance=100 package="0805 [SMD]"]

nets:
  N1: VCC1.-, U5.NO
  N2: VCC1.+, BAT1.-
  N3: BAT1.+, Composant1.OFF
  N4: Composant1.ON, LED1.anode
  N5: LED1.cathode, U1.NO
  N6: U1.COIL2, R1.Pin_0
  N7: U1.MAIN, U2.MAIN, U3.MAIN, U4.MAIN
  N8: U2.COIL1, Composant2.D31
  N9: U4.COIL1, Composant2.D30
  N10: U5.COIL2, Composant3.A0, R2.Pin_1
  N11: Composant2.GND, R2.Pin_0
  N12: Composant2.5V, R1.Pin_1
